# Fritzing sketch Sketch_NodeMCU (saved by Fritzing 0.9.3b)
breadboards: 1

parts:
  U2 = NodeMCU V3.0
  DHT23 = Humidity and Temperature Sensor RHT03
  MQ-137 = MQ-9 breakout
  MH-RD_-_Control_Board2 = YL-83 Rain Sensor - Control Board
  MH-RD_-_Detection_Board2 = MH-RD Rain Sensor - Detection Board
  SDS13 = IC, SIP package, 7 pins [chip_label=SDS011]
  CD4051B2 = IC, DIP package, 16 pins [chip_label=CD4051B]
  MQ-139 = MQ-9 breakout

nets:
  N1: U2.D1, SDS13.pin1
  N2: U2.D2, SDS13.pin2
  VCC: U2.3V3, DHT23.Vcc, MH-RD_-_Control_Board2.VCC, CD4051B2.pin16
  N3: U2.GND#6, U2.GND#13, U2.GND#16, U2.GND#33, DHT23.GND_2, MH-RD_-_Control_Board2.GND
  N4: U2.D7, DHT23.Data-signal
  N5: U2.D8, CD4051B2.pin9
  N6: U2.RX, CD4051B2.pin10
  N7: U2.TX, CD4051B2.pin11
  VCC_2: U2.VU, MQ-137.VCC, SDS13.pin4, SDS13.pin5, MQ-139.VCC
  GND: U2.GND#41, MQ-137.GND, SDS13.pin3, CD4051B2.pin8, MQ-139.GND
  N8: U2.A0, CD4051B2.pin3
  N9: MQ-137.AO, CD4051B2.pin13
  N10: MH-RD_-_Control_Board2.AO, CD4051B2.pin15
  N11: MH-RD_-_Control_Board2.POS, MH-RD_-_Detection_Board2.POS
  N12: MH-RD_-_Control_Board2.NEG, MH-RD_-_Detection_Board2.NEG
  N13: CD4051B2.pin14, MQ-139.AO

custom parts:
  NodeMCU V3.0: ESP8266 based NodeMCU
  Humidity and Temperature Sensor RHT03: Digital relative humidity & temperature sensor DHT22
  MQ-9 breakout: SKU: 101284
  YL-83 Rain Sensor - Control Board: The YL-83 is a rain sensor that has more resistance when dry and less resistance when wet. The module runs at 5V.
  MH-RD Rain Sensor - Detection Board: The MH-RD is a rain sensor that has more resistance when dry and less resistance when wet. The module runs at 5V.
  MQ-9 breakout: SKU: 101284
